# Fritzing sketch tesuto-chuu (saved by Fritzing 0.9.3b)
breadboards: 1

parts:
  LED1 = RGB LED (com. anode, rbg) [package="5 mm [THT]"]
  Grove1 = Grove OLED 128x96
  S1 = Pushbutton [package="[THT]"]
  U1 = ESP8266 WiFi Module [part_number=ESP8266]
  R1 = Resistor [tolerance=±5% resistance=10k package=THT]
  R2 = Resistor [tolerance=±5% resistance=10k package=THT]
  R3 = Resistor [tolerance=±5% resistance=10k package=THT]
  R5 = Resistor [tolerance=±5% resistance=10k package=THT]
  C1 = Electrolytic Capacitor [capacitance=1µF package="100 mil [THT, electrolytic]"]

nets:
  GND: LED1.common_anode, Grove1.GND, U1.GND, R1.Pin_1, R3.Pin_1, C1.-
  VCC: LED1.blue_cathode, Grove1.VCC, S1.Pin_1, S1.Pin_2, U1.VCC, R2.Pin_1, R5.Pin_0, C1.+
  N1: LED1.green_cathode, U1.GPIO_14
  N2: Grove1.SDA, U1.GPIO_4
  N3: Grove1.SCL, U1.GPIO_5
  N4: S1.Pin_3, S1.Pin_4, U1.GPIO_12, R1.Pin_0
  N5: U1.GPIO_0, R2.Pin_0
  N6: U1.CH_PD, R5.Pin_1
  N7: U1.GPIO_15, R3.Pin_0

notes:
  3.3V
  PL9823
